# Fritzing sketch circuit (saved by Fritzing 0.9.9b)
breadboards: 2

parts:
  S1 = Tilt Switch [package=THT]
  LED1 = RGB LED (com. anode, rbg) [package="5 mm [THT]"]
  R1 = Resistor [tolerance=±5% resistance=220 package="2010 [SMD]"]
  R2 = Resistor [tolerance=±5% resistance=220 package="2010 [SMD]"]
  R3 = Resistor [tolerance=±5% resistance=220 package="2010 [SMD]"]
  Part1 = Arduino Uno (Rev3) - ICSP
  Part2 = OLED Color 0.96 inch 96x64 w microSD [part_number=684]
  IC1 = L293D [package=THT]
  Water_Level_Sensor = Water Level Sensor
  YwRobot_Power_Supply1 = YwRobot Breadboard Power Supply [part_number=545043]
  VCC1 = Battery block 9V  # not connected
  M1 = DC Motor
  R4 = Resistor [tolerance=±5% resistance=220 package="2010 [SMD]"]
  Q1 = NPN-Transistor [package="TO92 [THT]"]
  Part3 = KY-012 Active Buzzer Module [package="Breakout board"]
  R5 = Temperature Sensor (Thermistor) [thermistor_type=NTC package=THT]
  R6 = Resistor [tolerance=±5% resistance=10k package="0603 [SMD]"]

nets:
  GND: S1.Pin_1, LED1.blue_cathode, Part1.GND, Part2.GND, IC1.0V, Water_Level_Sensor.GND, YwRobot_Power_Supply1.GND#11, YwRobot_Power_Supply1.GND#12, Part3.-, R6.Pin_0
  N1: S1.Pin_2, Part1.A2
  N2: LED1.red_cathode, R3.Pin_1
  N3: LED1.common_anode, R2.Pin_1
  N4: LED1.green_cathode, R1.Pin_1
  N5: R1.Pin_0, Part1.D2
  N6: R2.Pin_0, Part1.D3_PWM
  N7: R3.Pin_0, Part1.D4
  N8: Part1.A0, R5.pin_1, R6.Pin_1
  N9: Part1.A1, Water_Level_Sensor.SIG
  N10: Part1.D8, Part2.DC
  N11: Part1.D9_PWM, Part2.RESET
  N12: Part1.D10_PWM/SS, Part2.OLED_CS
  N13: Part1.D11_PWM/MOSI, Part2.MOSI
  N14: Part1.D12/MISO, R4.Pin_1
  N15: Part1.D13/SCK, Part2.SCK
  N16: Part1.D5_PWM, IC1.In_2
  N17: Part1.D6_PWM, IC1.In_1
  N18: Part1.D7, IC1.Enable_1
  5V: Part1.5V, Part2.V+, Water_Level_Sensor.VCC, R5.pin_0
  N19: IC1.Out_1_(_Controlled_by_Enable_1_), M1.pin_1
  N20: IC1.Out_2_(_Controlled_by_Enable_1_), M1.pin_2
  N21: IC1.+Vmotor, YwRobot_Power_Supply1.VCC#5, YwRobot_Power_Supply1.VCC#6, Q1.C
  N22: YwRobot_Power_Supply1.VCC#9, YwRobot_Power_Supply1.VCC#10
  N23: YwRobot_Power_Supply1.GND#13, YwRobot_Power_Supply1.GND#14
  N24: R4.Pin_0, Q1.B
  N25: Q1.E, Part3.S

custom parts:
  OLED Color 0.96 inch 96x64 w microSD: The visible portion of this OLED measures 0.96" diagonal and contains 96x64 RGB pixels, each one made of red, green and blue OLEDs. Each pixel can be set with 16-bits of resolution for a large range of colors. Because the display uses OLEDs, there is no backlight, and the contrast is very high (black is really black). We picked this display for its excellent color, this is the nicest mini OLED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
  Water Level Sensor: A water level sensor. This sensor operates at 3V to 5V. The Sig (signal) pin outputs an analogue signal that is in proportion to the amount of water in contact with the sensor.
  YwRobot Breadboard Power Supply: The YwRobot Breadboard Power Supply (MB-V2) has two power rails; they can be 5V or 3V3. Power to the module can be provided through the female USB socket or through the A10 (female) 2.1mm power jack.
  KY-012 Active Buzzer Module: Active Piezoelectric Buzzer Module Keyes KY-012, it produces single-tone sound when signal is high.
